// Digital circuit MUX_8bit.dig as structural Verilog
module MUX_8bit (
  input  INA0_LSB,
  input  INA1,
  input  INA2,
  input  INA3,
  input  INA4,
  input  INA5,
  input  INA6,
  input  INA7,
  input  INB0_LSB,
  input  INB1,
  input  INB2,
  input  INB3,
  input  INB4,
  input  INB5,
  input  INB6,
  input  INB7,
  input  S,
  output OUT0_LSB,
  output OUT1,
  output OUT2,
  output OUT3,
  output OUT4,
  output OUT5,
  output OUT6,
  output OUT7
);

  Multiplexer multiplexer_1 (.sel(S), .in_0(INA0_LSB), .in_1(INB0_LSB), .out(OUT0_LSB));
  Multiplexer multiplexer_2 (.sel(S), .in_0(INA1), .in_1(INB1), .out(OUT1));
  Multiplexer multiplexer_3 (.sel(S), .in_0(INA2), .in_1(INB2), .out(OUT2));
  Multiplexer multiplexer_4 (.sel(S), .in_0(INA3), .in_1(INB3), .out(OUT3));
  Multiplexer multiplexer_5 (.sel(S), .in_0(INA4), .in_1(INB4), .out(OUT4));
  Multiplexer multiplexer_6 (.sel(S), .in_0(INA5), .in_1(INB5), .out(OUT5));
  Multiplexer multiplexer_7 (.sel(S), .in_0(INA6), .in_1(INB6), .out(OUT6));
  Multiplexer multiplexer_8 (.sel(S), .in_0(INA7), .in_1(INB7), .out(OUT7));
endmodule
