// Digital circuit ULA.dig as structural Verilog
module ULA (
  input  INA0_LSB,
  input  INA1,
  input  INA2,
  input  INA3,
  input  INA4,
  input  INA5,
  input  INA6,
  input  INA7,
  input  INB0_LSB,
  input  INB1,
  input  INB2,
  input  INB3,
  input  INB4,
  input  INB5,
  input  INB6,
  input  INB7,
  input  Sel,
  output OUT0_LSB,
  output OUT1,
  output OUT2,
  output OUT3,
  output OUT4,
  output OUT5,
  output OUT6,
  output OUT7
);

  wire half_adder_8bit_1_out0__lsb, half_adder_8bit_1_out1, half_adder_8bit_1_out2, half_adder_8bit_1_out3,
       half_adder_8bit_1_out4, half_adder_8bit_1_out5, half_adder_8bit_1_out6, half_adder_8bit_1_out7,
       half_subtractor_8bit_1_out0__lsb, half_subtractor_8bit_1_out1, half_subtractor_8bit_1_out2,
       half_subtractor_8bit_1_out3, half_subtractor_8bit_1_out4, half_subtractor_8bit_1_out5,
       half_subtractor_8bit_1_out6, half_subtractor_8bit_1_out7;

  half_adder_8bit half_adder_8bit_1 (
    .A0__LSB(INA0_LSB), .A1(INA1), .A2(INA2), .A3(INA3), .A4(INA4), .A5(INA5), .A6(INA6), .A7(INA7),
    .B0__LSB(INB0_LSB), .B1(INB1), .B2(INB2), .B3(INB3), .B4(INB4), .B5(INB5), .B6(INB6), .B7(INB7),
    .OUT7(half_adder_8bit_1_out7), .OUT6(half_adder_8bit_1_out6), .OUT5(half_adder_8bit_1_out5),
    .OUT4(half_adder_8bit_1_out4), .OUT3(half_adder_8bit_1_out3), .OUT2(half_adder_8bit_1_out2),
    .OUT1(half_adder_8bit_1_out1), .OUT0__LSB(half_adder_8bit_1_out0__lsb));  // open: OUT8__COUT
  half_subtractor_8bit half_subtractor_8bit_1 (
    .A0__LSB(INA0_LSB), .A1(INA1), .A2(INA2), .A3(INA3), .A4(INA4), .A5(INA5), .A6(INA6), .A7(INA7),
    .B0__LSB(INB0_LSB), .B1(INB1), .B2(INB2), .B3(INB3), .B4(INB4), .B5(INB5), .B6(INB6), .B7(INB7),
    .OUT7(half_subtractor_8bit_1_out7), .OUT6(half_subtractor_8bit_1_out6),
    .OUT5(half_subtractor_8bit_1_out5), .OUT4(half_subtractor_8bit_1_out4),
    .OUT3(half_subtractor_8bit_1_out3), .OUT2(half_subtractor_8bit_1_out2),
    .OUT1(half_subtractor_8bit_1_out1), .OUT0__LSB(half_subtractor_8bit_1_out0__lsb));  // open: OUT8__COUT
  MUX_8bit mux_8bit_1 (
    .INA0_LSB(half_adder_8bit_1_out0__lsb), .INA1(half_adder_8bit_1_out1), .INA2(half_adder_8bit_1_out2),
    .INA3(half_adder_8bit_1_out3), .INA4(half_adder_8bit_1_out4), .INA5(half_adder_8bit_1_out5),
    .INA6(half_adder_8bit_1_out6), .INA7(half_adder_8bit_1_out7),
    .INB0_LSB(half_subtractor_8bit_1_out0__lsb), .INB1(half_subtractor_8bit_1_out1),
    .INB2(half_subtractor_8bit_1_out2), .INB3(half_subtractor_8bit_1_out3),
    .INB4(half_subtractor_8bit_1_out4), .INB5(half_subtractor_8bit_1_out5),
    .INB6(half_subtractor_8bit_1_out6), .INB7(half_subtractor_8bit_1_out7), .S(Sel), .OUT0_LSB(OUT0_LSB),
    .OUT1(OUT1), .OUT2(OUT2), .OUT3(OUT3), .OUT4(OUT4), .OUT5(OUT5), .OUT6(OUT6), .OUT7(OUT7));
endmodule
