// Digital circuit comparator_x_50.dig as structural Verilog
module comparator_x_50 (
  input  a,
  input  b,
  input  c,
  input  d,
  input  e,
  input  f,
  input  g,
  input  h,
  output OUT
);

  wire and_1_out, and_2_out, and_3_out, and_4_out, and_5_out, and_6_out, and_7_out, and_8_out, and_9_out,
       and_10_out, and_11_out, and_12_out, and_13_out, and_14_out, and_15_out, and_16_out, and_17_out,
       and_18_out, and_19_out, and_20_out, and_21_out, and_22_out, and_23_out, and_24_out, and_25_out,
       and_26_out, and_27_out, and_28_out, and_29_out, and_30_out, and_31_out, and_32_out, and_33_out,
       and_34_out, and_35_out, and_36_out, and_37_out, and_38_out, and_39_out, and_40_out, and_41_out,
       and_42_out, and_43_out, and_44_out, and_45_out, and_46_out, and_47_out, and_48_out, and_49_out,
       and_50_out, and_51_out, and_52_out, and_53_out, and_54_out, and_55_out, and_56_out, and_57_out,
       and_58_out, and_59_out, and_60_out, and_61_out, and_62_out, and_63_out, and_64_out, not_1_out,
       not_2_out, not_3_out, not_4_out, not_5_out, not_6_out, not_7_out, not_8_out, not_9_out, not_10_out,
       not_11_out, not_12_out, not_13_out, not_14_out, not_15_out, or_1_out, or_2_out, or_3_out, or_4_out,
       or_5_out, or_6_out, or_7_out, or_8_out, or_9_out, or_10_out, or_11_out, or_12_out, or_13_out,
       or_14_out, or_15_out, or_16_out, or_17_out, or_18_out, or_19_out, or_20_out, or_21_out, or_22_out,
       or_23_out, or_24_out, or_25_out, or_26_out, or_27_out, or_28_out;

  not not_1 (not_1_out, a);
  not not_2 (not_2_out, b);
  not not_3 (not_3_out, c);
  not not_4 (not_4_out, d);
  not not_5 (not_5_out, e);
  not not_6 (not_6_out, f);
  not not_7 (not_7_out, g);
  not not_8 (not_8_out, 1'b0);
  not not_9 (not_9_out, 1'b0);
  not not_10 (not_10_out, 1'b1);
  not not_11 (not_11_out, 1'b1);
  not not_12 (not_12_out, 1'b0);
  not not_13 (not_13_out, 1'b0);
  not not_14 (not_14_out, 1'b0);
  not not_15 (not_15_out, 1'b1);
  and and_1 (and_1_out, a, not_8_out);
  and and_2 (and_2_out, a, 1'b0);
  and and_3 (and_3_out, not_1_out, not_8_out);
  and and_4 (and_4_out, a, 1'b0);
  and and_5 (and_5_out, not_1_out, not_8_out);
  and and_6 (and_6_out, b, 1'b0);
  and and_7 (and_7_out, not_2_out, not_9_out);
  and and_8 (and_8_out, a, 1'b0);
  and and_9 (and_9_out, not_1_out, not_8_out);
  and and_10 (and_10_out, b, 1'b0);
  and and_11 (and_11_out, not_2_out, not_9_out);
  and and_12 (and_12_out, c, 1'b1);
  and and_13 (and_13_out, not_3_out, not_10_out);
  and and_14 (and_14_out, a, 1'b0);
  and and_15 (and_15_out, not_1_out, not_8_out);
  and and_16 (and_16_out, b, 1'b0);
  and and_17 (and_17_out, not_2_out, not_9_out);
  and and_18 (and_18_out, c, 1'b1);
  and and_19 (and_19_out, not_3_out, not_10_out);
  and and_20 (and_20_out, d, 1'b1);
  and and_21 (and_21_out, not_4_out, not_11_out);
  and and_22 (and_22_out, a, 1'b0);
  and and_23 (and_23_out, not_1_out, not_8_out);
  and and_24 (and_24_out, b, 1'b0);
  and and_25 (and_25_out, not_2_out, not_9_out);
  and and_26 (and_26_out, c, 1'b1);
  and and_27 (and_27_out, not_3_out, not_10_out);
  and and_28 (and_28_out, d, 1'b1);
  and and_29 (and_29_out, not_4_out, not_11_out);
  and and_30 (and_30_out, e, 1'b0);
  and and_31 (and_31_out, not_5_out, not_12_out);
  and and_32 (and_32_out, a, 1'b0);
  and and_33 (and_33_out, not_1_out, not_8_out);
  and and_34 (and_34_out, b, 1'b0);
  and and_35 (and_35_out, not_2_out, not_9_out);
  and and_36 (and_36_out, c, 1'b1);
  and and_37 (and_37_out, not_3_out, not_10_out);
  and and_38 (and_38_out, d, 1'b1);
  and and_39 (and_39_out, not_4_out, not_11_out);
  and and_40 (and_40_out, e, 1'b0);
  and and_41 (and_41_out, not_5_out, not_12_out);
  and and_42 (and_42_out, f, 1'b0);
  and and_43 (and_43_out, not_6_out, not_13_out);
  and and_44 (and_44_out, a, 1'b0);
  and and_45 (and_45_out, not_1_out, not_8_out);
  and and_46 (and_46_out, b, 1'b0);
  and and_47 (and_47_out, not_2_out, not_9_out);
  and and_48 (and_48_out, c, 1'b1);
  and and_49 (and_49_out, not_3_out, not_10_out);
  and and_50 (and_50_out, d, 1'b1);
  and and_51 (and_51_out, not_4_out, not_11_out);
  and and_52 (and_52_out, e, 1'b0);
  and and_53 (and_53_out, not_5_out, not_12_out);
  and and_54 (and_54_out, f, 1'b0);
  and and_55 (and_55_out, not_6_out, not_13_out);
  and and_56 (and_56_out, g, 1'b0);
  and and_57 (and_57_out, not_7_out, not_14_out);
  or or_1 (or_1_out, and_2_out, and_3_out);
  or or_2 (or_2_out, and_4_out, and_5_out);
  or or_3 (or_3_out, and_6_out, and_7_out);
  or or_4 (or_4_out, and_8_out, and_9_out);
  or or_5 (or_5_out, and_10_out, and_11_out);
  or or_6 (or_6_out, and_12_out, and_13_out);
  or or_7 (or_7_out, and_14_out, and_15_out);
  or or_8 (or_8_out, and_16_out, and_17_out);
  or or_9 (or_9_out, and_18_out, and_19_out);
  or or_10 (or_10_out, and_20_out, and_21_out);
  or or_11 (or_11_out, and_22_out, and_23_out);
  or or_12 (or_12_out, and_24_out, and_25_out);
  or or_13 (or_13_out, and_26_out, and_27_out);
  or or_14 (or_14_out, and_28_out, and_29_out);
  or or_15 (or_15_out, and_30_out, and_31_out);
  or or_16 (or_16_out, and_32_out, and_33_out);
  or or_17 (or_17_out, and_34_out, and_35_out);
  or or_18 (or_18_out, and_36_out, and_37_out);
  or or_19 (or_19_out, and_38_out, and_39_out);
  or or_20 (or_20_out, and_40_out, and_41_out);
  or or_21 (or_21_out, and_42_out, and_43_out);
  or or_22 (or_22_out, and_44_out, and_45_out);
  or or_23 (or_23_out, and_46_out, and_47_out);
  or or_24 (or_24_out, and_48_out, and_49_out);
  or or_25 (or_25_out, and_50_out, and_51_out);
  or or_26 (or_26_out, and_52_out, and_53_out);
  or or_27 (or_27_out, and_54_out, and_55_out);
  or or_28 (or_28_out, and_56_out, and_57_out);
  and and_58 (and_58_out, or_1_out, b, not_9_out);
  and and_59 (and_59_out, or_2_out, or_3_out, c, not_10_out);
  and and_60 (and_60_out, or_4_out, or_5_out, or_6_out, d, not_11_out);
  and and_61 (and_61_out, or_7_out, or_8_out, or_9_out, or_10_out, e, not_12_out);
  and and_62 (and_62_out, or_11_out, or_12_out, or_13_out, or_14_out, or_15_out, f, not_13_out);
  and and_63 (and_63_out, or_16_out, or_17_out, or_18_out, or_19_out, or_20_out, or_21_out, g, not_14_out);
  and and_64 (and_64_out, or_22_out, or_23_out, or_24_out, or_25_out, or_26_out, or_27_out, or_28_out, h, not_15_out);
  or or_29 (OUT, and_1_out, and_58_out, and_59_out, and_60_out, and_61_out, and_62_out, and_63_out, and_64_out);
endmodule
