// Digital circuit encoder_10x4.dig as structural Verilog
module encoder_10x4 (
  input  IN0__LSB,
  input  IN2,
  input  IN5,
  input  IN6,
  input  IN1,
  input  IN3,
  input  IN4,
  input  IN7,
  input  IN8,
  input  IN9,
  output OUT0__LSB,
  output OUT1,
  output OUT2,
  output OUT3
);

  or or_1 (OUT0__LSB, IN1, IN3, IN5, IN7, IN9);
  or or_2 (OUT1, IN2, IN3, IN6, IN7);
  or or_3 (OUT2, IN4, IN5, IN6, IN7);
  or or_4 (OUT3, IN8, IN9);
endmodule
