// Digital circuit half_subtractor_8bit.dig as structural Verilog
module half_subtractor_8bit (
  input  A0__LSB,
  input  B0__LSB,
  input  A1,
  input  A2,
  input  A3,
  input  A4,
  input  A5,
  input  A6,
  input  A7,
  input  B1,
  input  B2,
  input  B3,
  input  B4,
  input  B5,
  input  B6,
  input  B7,
  output OUT8__COUT,
  output OUT7,
  output OUT6,
  output OUT5,
  output OUT4,
  output OUT3,
  output OUT2,
  output OUT1,
  output OUT0__LSB
);

  wire sub_1_c_o, sub_2_c_o, sub_3_c_o, sub_4_c_o, sub_5_c_o, sub_6_c_o, sub_7_c_o;

  Sub sub_1 (.a(A0__LSB), .b(B0__LSB), .c_i(1'b0), .s(OUT0__LSB), .c_o(sub_1_c_o));
  Sub sub_2 (.a(A1), .b(B1), .c_i(sub_1_c_o), .s(OUT1), .c_o(sub_2_c_o));
  Sub sub_3 (.a(A2), .b(B2), .c_i(sub_2_c_o), .s(OUT2), .c_o(sub_3_c_o));
  Sub sub_4 (.a(A3), .b(B3), .c_i(sub_3_c_o), .s(OUT3), .c_o(sub_4_c_o));
  Sub sub_5 (.a(A4), .b(B4), .c_i(sub_4_c_o), .s(OUT4), .c_o(sub_5_c_o));
  Sub sub_6 (.a(A5), .b(B5), .c_i(sub_5_c_o), .s(OUT5), .c_o(sub_6_c_o));
  Sub sub_7 (.a(A6), .b(B6), .c_i(sub_6_c_o), .s(OUT6), .c_o(sub_7_c_o));
  Sub sub_8 (.a(A7), .b(B7), .c_i(sub_7_c_o), .s(OUT7), .c_o(OUT8__COUT));
endmodule
