// Digital circuit main.dig as structural Verilog
module main (
);

  wire main_black_box_1_da, main_black_box_1_db, main_black_box_1_dc, main_black_box_1_dd,
       main_black_box_1_de, main_black_box_1_df, main_black_box_1_dg, main_black_box_1_end,
       main_black_box_1_ua, main_black_box_1_ub, main_black_box_1_uc, main_black_box_1_ud,
       main_black_box_1_ue, main_black_box_1_uf, main_black_box_1_ug, plus_1_out, plus_2_out, plus_3_out,
       plus_5_out, plus_7_out, Undo_out;

  main_black_box main_black_box_1 (
    .plus_1(plus_1_out), .plus_2(plus_2_out), .plus_3(plus_3_out), .plus_5(plus_5_out), .plus_7(plus_7_out),
    .Undo(Undo_out), .Da(main_black_box_1_da), .Db(main_black_box_1_db), .Dc(main_black_box_1_dc),
    .Dd(main_black_box_1_dd), .De(main_black_box_1_de), .Df(main_black_box_1_df), .Dg(main_black_box_1_dg),
    .Ua(main_black_box_1_ua), .Ub(main_black_box_1_ub), .Uc(main_black_box_1_uc), .Ud(main_black_box_1_ud),
    .Ue(main_black_box_1_ue), .Uf(main_black_box_1_uf), .Ug(main_black_box_1_ug), .END(main_black_box_1_end));
  Button plus_1 (.out(plus_1_out));
  Button plus_2 (.out(plus_2_out));
  Button plus_3 (.out(plus_3_out));
  Button plus_5 (.out(plus_5_out));
  Button plus_7 (.out(plus_7_out));
  Button Undo (.out(Undo_out));
  Seven_Seg seven_seg_1 (
    .a(main_black_box_1_da), .b(main_black_box_1_db), .c(main_black_box_1_dc), .d(main_black_box_1_dd),
    .e(main_black_box_1_de), .f(main_black_box_1_df), .g(main_black_box_1_dg), .dp(1'b0));
  LED led_1 (.in(main_black_box_1_end));
  Seven_Seg seven_seg_2 (
    .a(main_black_box_1_ua), .b(main_black_box_1_ub), .c(main_black_box_1_uc), .d(main_black_box_1_ud),
    .e(main_black_box_1_ue), .f(main_black_box_1_uf), .g(main_black_box_1_ug), .dp(1'b0));
endmodule
