// Digital circuit main_black_box.dig as structural Verilog
module main_black_box (
  input  plus_1,
  input  plus_2,
  input  plus_3,
  input  plus_5,
  input  plus_7,
  input  Undo,
  output Da,
  output Db,
  output Dc,
  output Dd,
  output De,
  output Df,
  output Dg,
  output END,
  output Ua,
  output Ub,
  output Uc,
  output Ud,
  output Ue,
  output Uf,
  output Ug
);

  wire decoder_8x21_1_ca, decoder_8x21_1_cb, decoder_8x21_1_cc, decoder_8x21_1_cd, decoder_8x21_1_ce,
       decoder_8x21_1_cf, decoder_8x21_1_cg, encoder_10x4_1_out0__lsb, encoder_10x4_1_out1,
       encoder_10x4_1_out2, encoder_10x4_1_out3, nor_1_out, or_1_out, register_8bit_1_out_0__lsb,
       register_8bit_1_out_1, register_8bit_1_out_2, register_8bit_1_out_3, register_8bit_2_out_0__lsb,
       register_8bit_2_out_1, register_8bit_2_out_2, register_8bit_2_out_3, register_8bit_2_out_4,
       register_8bit_2_out_5, register_8bit_2_out_6, register_8bit_2_out_7, rs_ff_as_1_q, ula_1_out0_lsb,
       ula_1_out1, ula_1_out2, ula_1_out3, ula_1_out4, ula_1_out5, ula_1_out6, ula_1_out7;

  encoder_10x4 encoder_10x4_1 (
    .IN0__LSB(1'b0), .IN1(plus_1), .IN2(plus_2), .IN3(plus_3), .IN4(1'b0), .IN5(plus_5), .IN6(1'b0),
    .IN7(plus_7), .IN8(1'b0), .IN9(1'b0), .OUT0__LSB(encoder_10x4_1_out0__lsb), .OUT1(encoder_10x4_1_out1),
    .OUT2(encoder_10x4_1_out2), .OUT3(encoder_10x4_1_out3));
  or or_1 (or_1_out, encoder_10x4_1_out0__lsb, encoder_10x4_1_out1, encoder_10x4_1_out2, encoder_10x4_1_out3);
  nor nor_1 (nor_1_out, or_1_out, Undo);
  register_8bit register_8bit_1 (
    .R(or_1_out), .IN0__LSB(encoder_10x4_1_out0__lsb), .IN1(encoder_10x4_1_out1), .IN2(encoder_10x4_1_out2),
    .IN3(encoder_10x4_1_out3), .IN4(1'b0), .IN5(1'b0), .IN6(1'b0), .IN7(1'b0),
    .OUT_0__LSB(register_8bit_1_out_0__lsb), .OUT_1(register_8bit_1_out_1), .OUT_2(register_8bit_1_out_2),
    .OUT_3(register_8bit_1_out_3));  // open: OUT_4, OUT_5, OUT_6, OUT_7
  register_8bit register_8bit_2 (
    .R(nor_1_out), .IN0__LSB(ula_1_out0_lsb), .IN1(ula_1_out1), .IN2(ula_1_out2), .IN3(ula_1_out3),
    .IN4(ula_1_out4), .IN5(ula_1_out5), .IN6(ula_1_out6), .IN7(ula_1_out7),
    .OUT_0__LSB(register_8bit_2_out_0__lsb), .OUT_1(register_8bit_2_out_1), .OUT_2(register_8bit_2_out_2),
    .OUT_3(register_8bit_2_out_3), .OUT_4(register_8bit_2_out_4), .OUT_5(register_8bit_2_out_5),
    .OUT_6(register_8bit_2_out_6), .OUT_7(register_8bit_2_out_7));
  RS_FF_AS rs_ff_as_1 (.S(Undo), .R(or_1_out), .Q(rs_ff_as_1_q));  // open: nQ
  decoder_8x21 decoder_8x21_1 (
    .IN7(register_8bit_2_out_7), .IN6(register_8bit_2_out_6), .IN5(register_8bit_2_out_5),
    .IN4(register_8bit_2_out_4), .IN3(register_8bit_2_out_3), .IN2(register_8bit_2_out_2),
    .IN1(register_8bit_2_out_1), .IN0(register_8bit_2_out_0__lsb), .Ca(decoder_8x21_1_ca),
    .Cb(decoder_8x21_1_cb), .Cc(decoder_8x21_1_cc), .Cd(decoder_8x21_1_cd), .Ce(decoder_8x21_1_ce),
    .Cf(decoder_8x21_1_cf), .Cg(decoder_8x21_1_cg), .Da(Da), .Db(Db), .Dc(Dc), .Dd(Dd), .De(De), .Df(Df),
    .Dg(Dg), .Ua(Ua), .Ub(Ub), .Uc(Uc), .Ud(Ud), .Ue(Ue), .Uf(Uf), .Ug(Ug));
  comparator_x_50 comparator_x_50_1 (
    .a(register_8bit_2_out_7), .b(register_8bit_2_out_6), .c(register_8bit_2_out_5),
    .d(register_8bit_2_out_4), .e(register_8bit_2_out_3), .f(register_8bit_2_out_2),
    .g(register_8bit_2_out_1), .h(register_8bit_2_out_0__lsb), .OUT(END));
  ULA ula_1 (
    .INA0_LSB(register_8bit_2_out_0__lsb), .INA1(register_8bit_2_out_1), .INA2(register_8bit_2_out_2),
    .INA3(register_8bit_2_out_3), .INA4(register_8bit_2_out_4), .INA5(register_8bit_2_out_5),
    .INA6(register_8bit_2_out_6), .INA7(register_8bit_2_out_7), .INB0_LSB(register_8bit_1_out_0__lsb),
    .INB1(register_8bit_1_out_1), .INB2(register_8bit_1_out_2), .INB3(register_8bit_1_out_3), .INB4(1'b0),
    .INB5(1'b0), .INB6(1'b0), .INB7(1'b0), .Sel(rs_ff_as_1_q), .OUT0_LSB(ula_1_out0_lsb), .OUT1(ula_1_out1),
    .OUT2(ula_1_out2), .OUT3(ula_1_out3), .OUT4(ula_1_out4), .OUT5(ula_1_out5), .OUT6(ula_1_out6),
    .OUT7(ula_1_out7));
endmodule
