// Digital circuit register_8bit.dig as structural Verilog
module register_8bit (
  input  IN0__LSB,
  input  R,
  input  IN1,
  input  IN2,
  input  IN3,
  input  IN4,
  input  IN5,
  input  IN6,
  input  IN7,
  output OUT_0__LSB,
  output OUT_1,
  output OUT_2,
  output OUT_3,
  output OUT_4,
  output OUT_5,
  output OUT_6,
  output OUT_7
);

  Register register_1 (.D(IN0__LSB), .C(R), .en(R), .Q(OUT_0__LSB));
  Register register_2 (.D(IN1), .C(R), .en(R), .Q(OUT_1));
  Register register_3 (.D(IN2), .C(R), .en(R), .Q(OUT_2));
  Register register_4 (.D(IN3), .C(R), .en(R), .Q(OUT_3));
  Register register_5 (.D(IN4), .C(R), .en(R), .Q(OUT_4));
  Register register_6 (.D(IN5), .C(R), .en(R), .Q(OUT_5));
  Register register_7 (.D(IN6), .C(R), .en(R), .Q(OUT_6));
  Register register_8 (.D(IN7), .C(R), .en(R), .Q(OUT_7));
endmodule
